# Fritzing sketch 6x2-light-controller (saved by Fritzing 0.9.3b)
circuit board: 8.3992cm x 9.28258cm
breadboards: 1

parts:
  IC1 = ULN2803A [part_number=ULN2803A package=THT]
  IC2 = ULN2803A [part_number=ULN2803A package=THT]
  U1 = Sharp PC847X [part_number=TLP521-4 package=THT]
  R1 = Resistor [tolerance=±5% resistance=380 package=THT]
  R2 = Resistor [tolerance=±5% resistance=380 package=THT]
  R8 = Resistor [tolerance=±5% resistance=380 package=THT]
  R7 = Resistor [tolerance=±5% resistance=380 package=THT]
  R6 = Resistor [tolerance=±5% resistance=380 package=THT]
  R5 = Resistor [tolerance=±5% resistance=380 package=THT]
  R4 = Resistor [tolerance=±5% resistance=380 package=THT]
  R3 = Resistor [tolerance=±5% resistance=380 package=THT]
  R12 = Resistor [tolerance=±5% resistance=380 package=THT]
  R11 = Resistor [tolerance=±5% resistance=380 package=THT]
  R10 = Resistor [tolerance=±5% resistance=380 package=THT]
  R9 = Resistor [tolerance=±5% resistance=380 package=THT]
  U3 = Sharp PC847X [part_number=TLP521-4 package=THT]
  U2 = Sharp PC847X [part_number=TLP521-4 package=THT]
  J6 = Camdenboss CTB0158-12 [part_number=CTB0158-12 package=THT]
  J5 = Camdenboss CTB0158-2 [part_number=CTB0158-2 package=THT]
  J2 = Camdenboss CTB0158-8 [part_number=CTB0158-8 package=THT]
  J3 = Camdenboss CTB0158-2 [part_number=CTB0158-2 package=THT]
  J7 = Camdenboss CTB0158-12 [part_number=CTB0158-12 package=THT]
  J1 = Camdenboss CTB0158-8 [part_number=CTB0158-8 package=THT]
  J8 = female pin header, 2 pins [form="♀ (female)"]
  J9 = female pin header, 2 pins [form="♀ (female)"]

nets:
  N1: IC1.In_1, J1.pin1
  N2: IC1.In_2, J1.pin2
  N3: IC1.In_3, J1.pin3
  N4: IC1.In_4, J1.pin4
  N5: IC1.In_5, J1.pin5
  N6: IC1.In_6, J1.pin6
  N7: IC1.In_7, J1.pin7
  N8: IC1.In_8, J1.pin8
  GND: IC1.0V, IC2.0V, J3.pin2
  N9: IC1.Out_8, J8.pin2
  N10: IC1.Out_7, J8.pin1
  N11: IC1.Out_6, R6.Pin_0
  N12: IC1.Out_5, R5.Pin_0
  N13: IC1.Out_4, R4.Pin_0
  N14: IC1.Out_3, R3.Pin_0
  N15: IC1.Out_2, R2.Pin_0
  N16: IC1.Out_1, R1.Pin_0
  N17: IC2.In_1, J2.pin1
  N18: IC2.In_2, J2.pin2
  N19: IC2.In_3, J2.pin3
  N20: IC2.In_4, J2.pin4
  N21: IC2.In_5, J2.pin5
  N22: IC2.In_6, J2.pin6
  N23: IC2.In_7, J2.pin7
  N24: IC2.In_8, J2.pin8
  N25: IC2.Out_8, J9.pin2
  N26: IC2.Out_7, J9.pin1
  N27: IC2.Out_6, R12.Pin_0
  N28: IC2.Out_5, R11.Pin_0
  N29: IC2.Out_4, R10.Pin_0
  N30: IC2.Out_3, R9.Pin_0
  N31: IC2.Out_2, R8.Pin_0
  N32: IC2.Out_1, R7.Pin_0
  5V: U1.Pin_1, U1.Pin_3, U1.Pin_5, U1.Pin_7, U3.Pin_1, U3.Pin_3, U3.Pin_5, U3.Pin_7, U2.Pin_1, U2.Pin_3, U2.Pin_5, U2.Pin_7, J3.pin1
  N33: U1.Pin_2, R1.Pin_1
  N34: U1.Pin_4, R2.Pin_1
  N35: U1.Pin_6, R3.Pin_1
  N36: U1.Pin_8, R4.Pin_1
  3.3V: U1.Pin_9, U1.Pin_11, U1.Pin_13, U1.Pin_15, U3.Pin_9, U3.Pin_11, U3.Pin_13, U3.Pin_15, U2.Pin_9, U2.Pin_11, U2.Pin_13, U2.Pin_15, J5.pin2, J5.terminal_2
  N37: U1.Pin_10, J6.pin4
  N38: U1.Pin_12, J6.pin3
  N39: U1.Pin_14, J6.pin2
  N40: U1.Pin_16, J6.pin1
  N41: R8.Pin_1, U2.Pin_8
  N42: R7.Pin_1, U2.Pin_6
  N43: R6.Pin_1, U2.Pin_4
  N44: R5.Pin_1, U2.Pin_2
  N45: R12.Pin_1, U3.Pin_8
  N46: R11.Pin_1, U3.Pin_6
  N47: R10.Pin_1, U3.Pin_4
  N48: R9.Pin_1, U3.Pin_2
  N49: U3.Pin_10, J6.pin12
  N50: U3.Pin_12, J6.pin11
  N51: U3.Pin_14, J6.pin10
  N52: U3.Pin_16, J6.pin9
  N53: U2.Pin_10, J6.pin8
  N54: U2.Pin_12, J6.pin7
  N55: U2.Pin_14, J6.pin6
  N56: U2.Pin_16, J6.pin5
  12V: J5.pin1, J7.pin1, J7.pin2, J7.pin3, J7.pin4, J7.pin5, J7.pin6, J7.pin7, J7.pin8, J7.pin9, J7.pin10, J7.pin11, J7.pin12

notes:
  0V
  12V
  5V
  Lamps
  RPi GPIO
  Granta
  Traffic
  Lights
