# Fritzing sketch meeting-room-info (saved by Fritzing 0.9.3b)
circuit board: 3.85193cm x 5.80772cm
breadboards: 1

parts:
  Buttons = double row female pin header, 6 pins [form="♀ (female)"]
  Contrast = mystery part, 3 pins [chip_label=?]
  Backlight = mystery part, 3 pins [chip_label=?]
  R1 = Resistor [tolerance=±5% resistance=220 package=THT]
  RPi = mystery part, 40 pins [chip_label=?]
  LCD = mystery part, 18 pins [chip_label=?]
  R2 = Resistor [tolerance=±5% resistance=220 package=THT]
  Q1 = NPN-Transistor [package="TO92 [THT]"]
  Q2 = NPN-Transistor [package="TO92 [THT]"]
  R3 = Resistor [tolerance=±5% resistance=220 package=THT]
  R4 = Resistor [tolerance=±5% resistance=220 package=THT]
  Output = double row female pin header, 4 pins [form="♀ (female)"]
  PWR = female pin header, 2 pins [form="♀ (female)"]
  J2 = female pin header, 14 pins [form="♀ (female)"]

nets:
  N1: Buttons.pin1, RPi.pin28
  N2: Buttons.pin2, RPi.pin25
  N3: Buttons.pin3, RPi.pin23
  N4: Buttons.pin4, Buttons.pin5, Buttons.pin6, Contrast.pin3, RPi.pin34, RPi.pin38, LCD.pin7, LCD.pin10, LCD.pin14, Q1.E, Q2.E, PWR.pin2
  N5: Contrast.pin1, Backlight.pin1, RPi.pin39, RPi.pin40, LCD.pin12, Output.pin3, Output.pin4, PWR.pin1
  N6: Contrast.pin2, LCD.pin13
  N7: Backlight.pin2, LCD.pin9
  N8: R1.Pin_0, Q1.C
  N9: R1.Pin_1, Output.pin2
  N10: RPi.pin2, LCD.pin18
  N11: RPi.pin3, LCD.pin17
  N12: RPi.pin4, LCD.pin16
  N13: RPi.pin6, LCD.pin15
  N14: RPi.pin7, J2.pin1
  N15: RPi.pin8, J2.pin2
  N16: RPi.pin9, J2.pin3
  N17: RPi.pin10, J2.pin4
  N18: RPi.pin11, J2.pin5
  N19: RPi.pin12, J2.pin6
  N20: RPi.pin13, J2.pin7
  N21: RPi.pin14, J2.pin8
  N22: RPi.pin15, J2.pin9
  N23: RPi.pin16, J2.pin10
  N24: RPi.pin17, J2.pin11
  N25: RPi.pin18, J2.pin12
  N26: RPi.pin19, J2.pin13
  N27: RPi.pin20, J2.pin14
  N28: RPi.pin21, R4.Pin_0
  N29: RPi.pin22, R3.Pin_0
  N30: RPi.pin29, LCD.pin8
  N31: RPi.pin30, LCD.pin6
  N32: RPi.pin32, LCD.pin5
  N33: RPi.pin33, LCD.pin4
  N34: RPi.pin35, LCD.pin3
  N35: RPi.pin36, LCD.pin2
  N36: RPi.pin37, LCD.pin1
  N37: R2.Pin_0, Q2.C
  N38: R2.Pin_1, Output.pin1
  N39: Q1.B, R3.Pin_1
  N40: Q2.B, R4.Pin_1

notes:
  GND
  5V
