# Fritzing sketch traffic-light-controller (saved by Fritzing 0.9.3b)
circuit board: 12.3202cm x 14.984cm

parts:
  IC1 = ULN2803A [part_number=ULN2803A package=THT]
  U1 = Sharp PC847X [part_number=TLP521-4 package=THT]
  R1 = Resistor [tolerance=±5% resistance=100 package=THT]
  R2 = Resistor [tolerance=±5% resistance=100 package=THT]
  R8 = Resistor [tolerance=±5% resistance=100 package=THT]
  R7 = Resistor [tolerance=±5% resistance=100 package=THT]
  R6 = Resistor [tolerance=±5% resistance=100 package=THT]
  R5 = Resistor [tolerance=±5% resistance=100 package=THT]
  R4 = Resistor [tolerance=±5% resistance=100 package=THT]
  R3 = Resistor [tolerance=±5% resistance=100 package=THT]
  U2 = Sharp PC847X [part_number=TLP521-4 package=THT]
  J1 = shrouded pin header, 40 pins [form="♂ (shrouded male)" part_number=19-0530]
  LED1 = LED - 5mm [color="Green (555nm)" package="5 mm [THT]"]
  LED2 = LED - 5mm [color="Red (633nm)" package="5 mm [THT]"]
  LED3 = LED - 5mm [color="Green (555nm)" package="5 mm [THT]"]
  LED4 = LED - 5mm [color="Red (633nm)" package="5 mm [THT]"]
  LED5 = LED - 5mm [color="Green (555nm)" package="5 mm [THT]"]
  LED6 = LED - 5mm [color="Red (633nm)" package="5 mm [THT]"]
  LED7 = LED - 5mm [color="Green (555nm)" package="5 mm [THT]"]
  LED8 = LED - 5mm [color="Red (633nm)" package="5 mm [THT]"]
  LED15 = LED - 5mm [color="Green (555nm)" package="5 mm [THT]"]
  LED13 = LED - 5mm [color="Green (555nm)" package="5 mm [THT]"]
  LED11 = LED - 5mm [color="Green (555nm)" package="5 mm [THT]"]
  LED9 = LED - 5mm [color="Green (555nm)" package="5 mm [THT]"]
  LED16 = LED - 5mm [color="Red (633nm)" package="5 mm [THT]"]
  LED14 = LED - 5mm [color="Red (633nm)" package="5 mm [THT]"]
  LED12 = LED - 5mm [color="Red (633nm)" package="5 mm [THT]"]
  LED10 = LED - 5mm [color="Red (633nm)" package="5 mm [THT]"]
  IC2 = ULN2803A [part_number=ULN2803A package=THT]
  U4 = Sharp PC847X [part_number=TLP521-4 package=THT]
  U3 = Sharp PC847X [part_number=TLP521-4 package=THT]
  R11 = Resistor [tolerance=±5% resistance=100 package=THT]
  R12 = Resistor [tolerance=±5% resistance=100 package=THT]
  R13 = Resistor [tolerance=±5% resistance=100 package=THT]
  R14 = Resistor [tolerance=±5% resistance=100 package=THT]
  R15 = Resistor [tolerance=±5% resistance=100 package=THT]
  R16 = Resistor [tolerance=±5% resistance=100 package=THT]
  R10 = Resistor [tolerance=±5% resistance=100 package=THT]
  R9 = Resistor [tolerance=±5% resistance=100 package=THT]
  LED2_2 = LED - 5mm [color="Green (555nm)" package="5 mm [THT]"]
  LED21 = LED - 5mm [color="Green (555nm)" package="5 mm [THT]"]
  LED19 = LED - 5mm [color="Green (555nm)" package="5 mm [THT]"]
  LED17 = LED - 5mm [color="Green (555nm)" package="5 mm [THT]"]
  LED24 = LED - 5mm [color="Red (633nm)" package="5 mm [THT]"]
  LED22 = LED - 5mm [color="Red (633nm)" package="5 mm [THT]"]
  LED20 = LED - 5mm [color="Red (633nm)" package="5 mm [THT]"]
  LED18 = LED - 5mm [color="Red (633nm)" package="5 mm [THT]"]
  IC3 = ULN2803A [part_number=ULN2803A package=THT]
  U6 = Sharp PC847X [part_number=TLP521-4 package=THT]
  U5 = Sharp PC847X [part_number=TLP521-4 package=THT]
  R19 = Resistor [tolerance=±5% resistance=100 package=THT]
  R20 = Resistor [tolerance=±5% resistance=100 package=THT]
  R21 = Resistor [tolerance=±5% resistance=100 package=THT]
  R22 = Resistor [tolerance=±5% resistance=100 package=THT]
  R23 = Resistor [tolerance=±5% resistance=100 package=THT]
  R24 = Resistor [tolerance=±5% resistance=100 package=THT]
  R18 = Resistor [tolerance=±5% resistance=100 package=THT]
  R17 = Resistor [tolerance=±5% resistance=100 package=THT]
  Q1 = NPN-Transistor [part_number=BC547B package="TO92 [THT]"]
  B1 = mystery part, 3 pins [chip_label="Buzzer 2300Hz" part_number="35-3594 RVFM 3V electronic buzzer"]
  R25 = Resistor [tolerance=±5% resistance=10k package=THT]
  Q2 = NPN-Transistor [part_number=BC547B package="TO92 [THT]"]
  B2 = mystery part, 3 pins [chip_label="Buzzer 400Hz" part_number="35-0048 RVFM 5V minature electroinc buzzer"]
  R26 = Resistor [tolerance=±5% resistance=10k package=THT]
  J2 = screw terminal, 6 pins [part_number=CTB3008/6]
  J3 = screw terminal, 6 pins [part_number=CTB3008/6]
  J4 = screw terminal, 6 pins [part_number=CTB3008/6]
  J5 = screw terminal, 6 pins [part_number=CTB3008/6]
  J6 = screw terminal, 6 pins [part_number=CTB3008/6]
  J8 = screw terminal, 6 pins [part_number=CTB3008/6]
  J9 = screw terminal, 6 pins [part_number=CTB3008/6]
  J7 = screw terminal, 6 pins [part_number=CTB3008/6]
  Power_plug2 = Power plug
  S1 = SWITCH-MOMENTARY-2 [package=tactile-pth-12mm]

nets (from the pcb view):
  N1: IC1.In_1, J1.pin7
  N2: IC1.In_2, J1.pin6
  N3: IC1.In_3, J1.pin4
  N4: IC1.In_4, J1.pin3
  N5: IC1.In_5, J1.pin2
  N6: IC1.In_6, J1.pin37
  N7: IC1.In_7, J1.pin36
  N8: IC1.In_8, J1.pin35
  N9: IC1.0V, J1.pin38, IC2.0V, IC3.0V, Q2.E
  N10: IC1.Out_8, R8.Pin_0
  N11: IC1.Out_7, R7.Pin_0
  N12: IC1.Out_6, R6.Pin_0
  N13: IC1.Out_5, R5.Pin_0
  N14: IC1.Out_4, R4.Pin_0
  N15: IC1.Out_3, R3.Pin_0
  N16: IC1.Out_2, R2.Pin_0
  N17: IC1.Out_1, R1.Pin_0
  N18: U1.Pin_1, U1.Pin_3, U1.Pin_5, U1.Pin_7, U2.Pin_1, U2.Pin_3, U2.Pin_5, U2.Pin_7, J1.pin39, J1.pin40, U4.Pin_1, U4.Pin_3, U4.Pin_5, U4.Pin_7, U3.Pin_1, U3.Pin_3, U3.Pin_5, U3.Pin_7, U6.Pin_1, U6.Pin_3, U6.Pin_5, U6.Pin_7, U5.Pin_1, U5.Pin_3, U5.Pin_5, U5.Pin_7, B1.pin1, B2.pin1
  N19: U1.Pin_2, LED1.anode
  N20: U1.Pin_4, LED2.anode
  N21: U1.Pin_6, LED3.anode
  N22: U1.Pin_8, LED4.anode
  N23: U1.Pin_9, U1.Pin_11, U1.Pin_13, U1.Pin_15, U2.Pin_9, U2.Pin_11, U2.Pin_13, U2.Pin_15, U4.Pin_9, U4.Pin_11, U4.Pin_13, U4.Pin_15, U3.Pin_9, U3.Pin_11, U3.Pin_13, U3.Pin_15, U6.Pin_9, U6.Pin_11, U6.Pin_13, U6.Pin_15, U5.Pin_9, U5.Pin_11, U5.Pin_13, U5.Pin_15, Power_plug2.GND
  N24: U1.Pin_10, J2.pin4
  N25: U1.Pin_12, J2.pin3
  N26: U1.Pin_14, J2.pin2
  N27: U1.Pin_16, J2.pin1
  N28: R1.Pin_1, LED1.cathode
  N29: R2.Pin_1, LED2.cathode
  N30: R8.Pin_1, LED8.cathode
  N31: R7.Pin_1, LED7.cathode
  N32: R6.Pin_1, LED6.cathode
  N33: R5.Pin_1, LED5.cathode
  N34: R4.Pin_1, LED4.cathode
  N35: R3.Pin_1, LED3.cathode
  N36: U2.Pin_2, LED5.anode
  N37: U2.Pin_4, LED6.anode
  N38: U2.Pin_6, LED7.anode
  N39: U2.Pin_8, LED8.anode
  N40: U2.Pin_10, J3.pin2
  N41: U2.Pin_12, J3.pin1
  N42: U2.Pin_14, J2.pin6
  N43: U2.Pin_16, J2.pin5
  N44: J1.pin5, Q1.E
  N45: J1.pin8, R25.Pin_0
  N46: J1.pin10, R26.Pin_0
  N47: J1.pin12, S1.2
  N48: J1.pin13, S1.1
  N49: J1.pin14, IC3.In_8
  N50: J1.pin15, IC3.In_7
  N51: J1.pin16, IC3.In_6
  N52: J1.pin17, IC3.In_5
  N53: J1.pin18, IC3.In_4
  N54: J1.pin19, IC3.In_3
  N55: J1.pin21, IC3.In_2
  N56: J1.pin22, IC3.In_1
  N57: J1.pin23, IC2.In_8
  N58: J1.pin25, IC2.In_7
  N59: J1.pin27, IC2.In_6
  N60: J1.pin28, IC2.In_5
  N61: J1.pin29, IC2.In_4
  N62: J1.pin30, IC2.In_3
  N63: J1.pin32, IC2.In_2
  N64: J1.pin33, IC2.In_1
  N65: LED15.cathode, R15.Pin_1
  N66: LED15.anode, U4.Pin_6
  N67: LED13.cathode, R13.Pin_1
  N68: LED13.anode, U4.Pin_2
  N69: LED11.cathode, R11.Pin_1
  N70: LED11.anode, U3.Pin_6
  N71: LED9.cathode, R9.Pin_1
  N72: LED9.anode, U3.Pin_2
  N73: LED16.cathode, R16.Pin_1
  N74: LED16.anode, U4.Pin_8
  N75: LED14.cathode, R14.Pin_1
  N76: LED14.anode, U4.Pin_4
  N77: LED12.cathode, R12.Pin_1
  N78: LED12.anode, U3.Pin_8
  N79: LED10.cathode, R10.Pin_1
  N80: LED10.anode, U3.Pin_4
  N81: IC2.Out_8, R16.Pin_0
  N82: IC2.Out_7, R15.Pin_0
  N83: IC2.Out_6, R14.Pin_0
  N84: IC2.Out_5, R13.Pin_0
  N85: IC2.Out_4, R12.Pin_0
  N86: IC2.Out_3, R11.Pin_0
  N87: IC2.Out_2, R10.Pin_0
  N88: IC2.Out_1, R9.Pin_0
  N89: U4.Pin_10, J4.pin4
  N90: U4.Pin_12, J4.pin3
  N91: U4.Pin_14, J4.pin2
  N92: U4.Pin_16, J4.pin1
  N93: U3.Pin_10, J3.pin6
  N94: U3.Pin_12, J3.pin5
  N95: U3.Pin_14, J3.pin4
  N96: U3.Pin_16, J3.pin3
  N97: LED2_2.cathode, R23.Pin_1
  N98: LED2_2.anode, U6.Pin_6
  N99: LED21.cathode, R21.Pin_1
  N100: LED21.anode, U6.Pin_2
  N101: LED19.cathode, R19.Pin_1
  N102: LED19.anode, U5.Pin_6
  N103: LED17.cathode, R17.Pin_1
  N104: LED17.anode, U5.Pin_2
  N105: LED24.cathode, R24.Pin_1
  N106: LED24.anode, U6.Pin_8
  N107: LED22.cathode, R22.Pin_1
  N108: LED22.anode, U6.Pin_4
  N109: LED20.cathode, R20.Pin_1
  N110: LED20.anode, U5.Pin_8
  N111: LED18.cathode, R18.Pin_1
  N112: LED18.anode, U5.Pin_4
  N113: IC3.Out_8, R24.Pin_0
  N114: IC3.Out_7, R23.Pin_0
  N115: IC3.Out_6, R22.Pin_0
  N116: IC3.Out_5, R21.Pin_0
  N117: IC3.Out_4, R20.Pin_0
  N118: IC3.Out_3, R19.Pin_0
  N119: IC3.Out_2, R18.Pin_0
  N120: IC3.Out_1, R17.Pin_0
  N121: U6.Pin_10, J5.pin6
  N122: U6.Pin_12, J5.pin5
  N123: U6.Pin_14, J5.pin4
  N124: U6.Pin_16, J5.pin3
  N125: U5.Pin_10, J5.pin2
  N126: U5.Pin_12, J5.pin1
  N127: U5.Pin_14, J4.pin6
  N128: U5.Pin_16, J4.pin5
  N129: Q1.B, R25.Pin_1
  N130: Q1.C, B1.pin3
  N131: Q2.B, R26.Pin_1
  N132: Q2.C, B2.pin3
  N133: J6.pin1, J6.pin2, J6.pin3, J6.pin4, J6.pin5, J6.pin6, J8.pin1, J8.pin2, J8.pin3, J8.pin4, J8.pin5, J8.pin6, J9.pin1, J9.pin2, J9.pin3, J9.pin4, J9.pin5, J9.pin6, J7.pin1, J7.pin2, J7.pin3, J7.pin4, J7.pin5, J7.pin6, Power_plug2.VCC

notes:
  12V
  RPi GPIO
  Note that header pinouts are labelled differently from jumper socket pinouts.
  See gpio pinout.txt for mapping between the two
  C+
  -  +
  Ø3mm @ 100 x 125

custom parts:
  Power plug: power plug
